# Fritzing sketch Gardnr_Module (saved by Fritzing 0.9.2b)
circuit board: 9cm x 6cm
breadboards: 1

parts:
  U3 = ESP8266 WiFi Module [part_number=ESP8266]
  VCC2 = Battery
  XTAL2 = Crystal [frequency="16 Mhz" package=THT]
  C3 = Ceramic Capacitor [capacitance=22pF package="100 mil [THT, multilayer]"]
  C4 = Ceramic Capacitor [capacitance=22pF package="100 mil [THT, multilayer]"]
  R7 = Resistor [tolerance=±5% resistance=100k package=THT]
  R8 = Resistor [tolerance=±5% resistance=10 package=THT]
  Moisture = Screw terminal - 2 pins [package=THT]
  R9 = Resistor [tolerance=±5% resistance=330 package=THT]
  R10 = Resistor [tolerance=±5% resistance=220 package=THT]
  PhotoSensor1 = Resistor [tolerance=±5% resistance=10k package=THT]
  DHT1 = DHT22 Humidity and Temperature Sensor
  R11 = Resistor [tolerance=±5% resistance=10k package=THT]
  Soil_Temp = Screw terminal - 2 pins [package=THT]
  U1 = atmega328 [package=dip]

nets:
  N1: U3.RXD, U1.D1_(TX)
  3.3V: U3.VCC, U3.CH_PD, VCC2.+, R9.Pin_1, R10.Pin_1, DHT1.VDD, R11.Pin_0, U1.VCC, U1.AVCC, U1.AREF
  GND: U3.GND, VCC2.-, C3.0, C4.0, PhotoSensor1.Pin_1, DHT1.GND, Soil_Temp.pin1, U1.GND
  N2: U3.TXD, U1.D0_(RX)
  N3: XTAL2.pin_0, C3.1, U1.XLAT1
  N4: XTAL2.pin_1, C4.1, U1.XLAT2
  N5: R7.Pin_0, Moisture.pin2
  Arduino A2: R7.Pin_1, U1.D8, U1.A2
  N6: R8.Pin_0, Moisture.pin1
  N7: R8.Pin_1, U1.D7
  Arduino A3: R9.Pin_0, Soil_Temp.pin2, U1.A3
  Arduino A1: R10.Pin_0, PhotoSensor1.Pin_0, U1.A1
  Arduino D2: DHT1.DATA, R11.Pin_1, U1.D2

notes:
  Light Sensor

custom parts:
  ESP8266 WiFi Module: Generic WiFi Module based on the ESP8266 with onboard PCB antenna and UART communications
